# Fritzing sketch 4WD RC Car (saved by Fritzing 0.9.2b)
breadboards: 1

parts:
  U1 = Bluetooth HC-05 Fêmea [part_number=3459898989898]  # not connected
  Part1 = Bluetooth HC-05 Macho
  Part2 = Arduino Uno (Rev3)
  M2 = DC Motor
  M3 = DC Motor
  M4 = DC Motor
  M5 = DC Motor
  S1 = H-Bridge with L298N
  R1 = Resistor [tolerance=±5% resistance=1k package=THT]
  R2 = Resistor [tolerance=±5% resistance=1k package=THT]
  R3 = Resistor [tolerance=±5% resistance=1k package=THT]
  9V = 4 x AAA Battery Mount

nets:
  N1: Part1.TXD, Part2.D3_PWM
  N2: Part1.RXD, R1.Pin_1, R2.Pin_0
  VCC: Part1.VCC, Part2.5V
  GND: Part1.GND, Part2.GND, S1.GND, R3.Pin_0, 9V.-
  N3: Part2.D9_PWM, S1.IN3
  N4: Part2.D10_PWM/SS, S1.IN2
  N5: Part2.D11_PWM/MOSI, S1.IN1
  N6: Part2.D4, R1.Pin_0
  N7: Part2.D6_PWM, S1.IN4
  VIN: Part2.VIN, S1.12V, 9V.+
  N8: M2.pin_1, M5.pin_1, S1.OUT2-Motor1
  N9: M2.pin_2, M5.pin_2, S1.OUT1-Motor1
  N10: M3.pin_1, M4.pin_1, S1.OUT3-Motor2
  N11: M3.pin_2, M4.pin_2, S1.OUT4-Motor2
  N12: R2.Pin_1, R3.Pin_1

notes:
  LEFT Motors
  RIGHT Motors
  makerspace-az.org

custom parts:
  Bluetooth HC-05 Fêmea: Bluetooth module uses HC-05
  H-Bridge with L298N: h-bridge
