# Fritzing sketch 4WD RC nRF24l01_RX (saved by Fritzing 0.9.2b)
breadboards: 1

parts:
  NRF24L1 = NRF24L01
  S1 = H-Bridge with L298N
  Batareya2 = 4 x AAA Battery Mount
  Batareya1 = 4 x AAA Battery Mount
  M1 = DC Motor
  M2 = DC Motor
  Pro_Mini = Arduino Uno (Rev3) - ICSP

nets:
  VCC: NRF24L1.VCC, Pro_Mini.3V3
  N1: NRF24L1.CSN, Pro_Mini.D10_PWM/SS
  N2: NRF24L1.MOSI, Pro_Mini.D11_PWM/MOSI
  GND: NRF24L1.GND, S1.GND, Batareya1.-, Pro_Mini.GND
  N3: NRF24L1.CE, Pro_Mini.D8
  N4: NRF24L1.SCK, Pro_Mini.D13/SCK
  N5: NRF24L1.MISO, Pro_Mini.D12/MISO
  12V: S1.12V, Batareya2.+, Pro_Mini.VIN
  N6: S1.IN1, Pro_Mini.D9_PWM
  N7: S1.IN2, Pro_Mini.D6_PWM
  N8: S1.IN3, Pro_Mini.D5_PWM
  N9: S1.IN4, Pro_Mini.D3_PWM
  N10: S1.OUT3-Motor2, M1.pin_2
  N11: S1.OUT4-Motor2, M1.pin_1
  N12: S1.OUT1-Motor1, M2.pin_1
  N13: S1.OUT2-Motor1, M2.pin_2
  N14: Batareya2.-, Batareya1.+

notes:
  makerspace-az.org

custom parts:
  NRF24L01: NRF24L01 module
  H-Bridge with L298N: h-bridge
