# Fritzing sketch 4WD_ROBOT_nRF24l01_TX (saved by Fritzing 0.9.2b)
breadboards: 1

parts:
  Pro_Mini_3_3V = Arduino Pro Mini v13
  NRF24L01 = NRF24L01
  4_8V = 4 x AAA Battery Mount
  Batareya = Thumb Joystick
  3_3V = Voltage Regulator - 5V [package="TO220 [THT]"]
  C1 = Electrolytic Capacitor [capacitance=10µF voltage=10V package="100 mil [THT, electrolytic]"]
  C2 = Electrolytic Capacitor [capacitance=10µF voltage=20V package="100 mil [THT, electrolytic]"]
  Elektrik_Achar = SWITCH_SPDT [package=kps-1290]

nets:
  VCC: Pro_Mini_3_3V.VCC, NRF24L01.VCC, Batareya.VCC, 3_3V.output_voltage, C1.+
  GND: Pro_Mini_3_3V.GND, NRF24L01.GND, 4_8V.-, Batareya.GND, 3_3V.GND, C1.-, C2.-
  N1: Pro_Mini_3_3V.A1, Batareya.VERT
  N2: Pro_Mini_3_3V.A0, Batareya.HORZ
  N3: Pro_Mini_3_3V.D13/SCK, NRF24L01.SCK
  N4: Pro_Mini_3_3V.D12/MISO, NRF24L01.MISO
  N5: Pro_Mini_3_3V.D11_PWM/MOSI, NRF24L01.MOSI
  N6: Pro_Mini_3_3V.D10_PWM/SS, NRF24L01.CSN
  N7: Pro_Mini_3_3V.D9_PWM, NRF24L01.CE
  N8: Pro_Mini_3_3V.D4, Batareya.SEL
  N9: 4_8V.+, Elektrik_Achar.P
  N10: 3_3V.input_voltage, C2.+, Elektrik_Achar.O

notes:
  Joystick
  makerspace-az.org

custom parts:
  NRF24L01: NRF24L01 module
