# Fritzing sketch Hbridge (saved by Fritzing 0.9.2b)

parts:
  M1 = DC Motor
  U1 = SWITCH-SPST-2 [package=switch-spst-vertical]
  U2 = SWITCH-SPST-2 [package=switch-spst-vertical]
  U3 = SWITCH-SPST-2 [package=switch-spst-vertical]
  U4 = SWITCH-SPST-2 [package=switch-spst-vertical]
  BAT-9V = BC9VPC [package=bc9vpc]

nets:
  N1: M1.pin_1, U2.O, U4.P
  N2: M1.pin_2, U1.O, U3.P
  N3: U1.P, U2.P, BAT-9V.V-
  N4: U3.O, U4.O, BAT-9V.V+

notes:
  makerspace-az.org
  +
  -
