# Fritzing sketch LED_Lamp_12V (saved by Fritzing 0.9.2b)
stripboards: 2

parts:
  LED1 = LEDs [package=fkit-led-1206]
  LED2 = LEDs [package=fkit-led-1206]
  LED3 = LEDs [package=fkit-led-1206]
  LED4 = LEDs [package=fkit-led-1206]
  LED5 = LEDs [package=fkit-led-1206]
  LED6 = LEDs [package=fkit-led-1206]
  LED7 = LEDs [package=fkit-led-1206]
  LED8 = LEDs [package=fkit-led-1206]
  LED9 = LEDs [package=fkit-led-1206]
  LED10 = LEDs [package=fkit-led-1206]
  LED11 = LEDs [package=fkit-led-1206]
  LED12 = LEDs [package=fkit-led-1206]
  LED13 = LEDs [package=fkit-led-1206]
  LED14 = LEDs [package=fkit-led-1206]
  LED15 = LEDs [package=fkit-led-1206]
  LED16 = LEDs [package=fkit-led-1206]
  LED17 = LEDs [package=fkit-led-1206]
  LED18 = LEDs [package=fkit-led-1206]
  LED19 = LEDs [package=fkit-led-1206]
  LED20 = LEDs [package=fkit-led-1206]
  LED21 = LEDs [package=fkit-led-1206]
  LED22 = LEDs [package=fkit-led-1206]
  LED23 = LEDs [package=fkit-led-1206]
  LED24 = LEDs [package=fkit-led-1206]
  LED25 = LEDs [package=fkit-led-1206]
  LED26 = LEDs [package=fkit-led-1206]
  LED27 = LEDs [package=fkit-led-1206]
  LED28 = LEDs [package=fkit-led-1206]
  LED29 = LEDs [package=fkit-led-1206]
  LED30 = LEDs [package=fkit-led-1206]
  LED31 = LEDs [package=fkit-led-1206]
  LED32 = LEDs [package=fkit-led-1206]
  LED33 = LEDs [package=fkit-led-1206]
  LED34 = LEDs [package=fkit-led-1206]
  LED35 = LEDs [package=fkit-led-1206]
  LED36 = LEDs [package=fkit-led-1206]
  LED37 = LEDs [package=fkit-led-1206]
  LED38 = LEDs [package=fkit-led-1206]
  LED39 = LEDs [package=fkit-led-1206]
  LED40 = LEDs [package=fkit-led-1206]
  R1 = Resistor [tolerance=±5% resistance=15 package="2512 [SMD]"]
  R2 = Resistor [tolerance=±5% resistance=15 package="2512 [SMD]"]
  R3 = Resistor [tolerance=±5% resistance=15 package="2512 [SMD]"]
  R4 = Resistor [tolerance=±5% resistance=15 package="2512 [SMD]"]
  R5 = Resistor [tolerance=±5% resistance=15 package="2512 [SMD]"]
  R6 = Resistor [tolerance=±5% resistance=15 package="2512 [SMD]"]
  R7 = Resistor [tolerance=±5% resistance=15 package="2512 [SMD]"]
  R8 = Resistor [tolerance=±5% resistance=15 package="2512 [SMD]"]
  R9 = Resistor [tolerance=±5% resistance=15 package="2512 [SMD]"]
  R10 = Resistor [tolerance=±5% resistance=15 package="2512 [SMD]"]
  S1 = Round Pushbutton
  12V = Battery block 9V

nets:
  N1: LED1.A, LED2.C
  N2: LED1.C, R1.Pin_0
  N3: LED2.A, LED3.C
  N4: LED3.A, LED4.C
  N5: LED4.A, LED5.A, LED9.A, LED13.A, LED17.A, LED21.A, LED25.A, LED29.A, LED33.A, LED37.A, S1.leg1
  N6: LED5.C, LED6.A
  N7: LED6.C, LED7.A
  N8: LED7.C, LED8.A
  N9: LED8.C, R2.Pin_0
  N10: LED9.C, LED10.A
  N11: LED10.C, LED11.A
  N12: LED11.C, LED12.A
  N13: LED12.C, R3.Pin_0
  N14: LED13.C, LED14.A
  N15: LED14.C, LED15.A
  N16: LED15.C, LED16.A
  N17: LED16.C, R4.Pin_0
  N18: LED17.C, LED18.A
  N19: LED18.C, LED19.A
  N20: LED19.C, LED20.A
  N21: LED20.C, R5.Pin_0
  N22: LED21.C, LED22.A
  N23: LED22.C, LED23.A
  N24: LED23.C, LED24.A
  N25: LED24.C, R6.Pin_0
  N26: LED25.C, LED26.A
  N27: LED26.C, LED27.A
  N28: LED27.C, LED28.A
  N29: LED28.C, R7.Pin_0
  N30: LED29.C, LED30.A
  N31: LED30.C, LED31.A
  N32: LED31.C, LED32.A
  N33: LED32.C, R8.Pin_0
  N34: LED33.C, LED34.A
  N35: LED34.C, LED35.A
  N36: LED35.C, LED36.A
  N37: LED36.C, R9.Pin_0
  N38: LED37.C, LED38.A
  N39: LED38.C, LED39.A
  N40: LED39.C, LED40.A
  N41: LED40.C, R10.Pin_0
  N42: R1.Pin_1, R2.Pin_1, R3.Pin_1, R4.Pin_1, R5.Pin_1, 12V.-
  N43: R6.Pin_1, R7.Pin_1, R8.Pin_1, R9.Pin_1, R10.Pin_1
  N44: S1.leg0, 12V.+

notes:
  Batareya əvəzinə 12V qida bloku
  makerspace-az.org
